# Fritzing sketch sketch (saved by Fritzing 0.9.3b)
breadboards: 1

parts:
  Part1 = Thumb Joystick
  Part2 = Thumb Joystick
  Part3 = Thumb Joystick
  Part4 = Thumb Joystick
  LCD2 = LCD screen
  LCM1602_IIC2 = LCM1602 IIC [part_number="LCM1602 IIC" chip_label="LCM1602 IIC" package="DIP (Dual Inline) [THT]"]
  S1 = Round Pushbutton
  Part5 = Arduino Micro (Rev3)
  S2 = Taiway 100-SP-X-T1 SPDT Miniature Toggle Switch [part_number=100-SP-X-T1-0-0-B1-M1 package=THT]
  U2 = PCF8574 [package="DIP16 [THT]"]
  U1 = PCF8574 [package="DIP16 [THT]"]
  S3 = Round Pushbutton
  S4 = Round Pushbutton
  S5 = Round Pushbutton
  S6 = Round Pushbutton
  S7 = Round Pushbutton
  LED3 = smd LED [color="Red (633nm)" package="0603 [SMD]"]
  LED4 = smd LED [color="Red (633nm)" package="0603 [SMD]"]
  LED5 = smd LED [color="Red (633nm)" package="0603 [SMD]"]
  LED6 = smd LED [color="Red (633nm)" package="0603 [SMD]"]
  LED7 = smd LED [color="Red (633nm)" package="0603 [SMD]"]
  LED2 = smd LED [color="Red (633nm)" package="0603 [SMD]"]
  R1 = Resistor [tolerance=±5% resistance=220 package=THT]
  R2 = Resistor [tolerance=±5% resistance=220 package=THT]
  R3 = Resistor [tolerance=±5% resistance=220 package=THT]
  R4 = Resistor [tolerance=±5% resistance=220 package=THT]
  R5 = Resistor [tolerance=±5% resistance=220 package=THT]
  R6 = Resistor [tolerance=±5% resistance=220 package=THT]

nets:
  GND: Part1.GND, Part2.GND, Part3.GND, Part4.GND, LCM1602_IIC2.GND, S1.leg1, S2.L2, U2.A1, U2.A2, U2.P2, U2.GND, U1.A0, U1.A1, U1.A2, U1.GND, S3.leg1, S4.leg1, S5.leg1, S6.leg1, S7.leg0, S7.leg1
  N1: Part1.SEL, Part5.D7
  N2: Part1.HORZ, Part5.A0
  N3: Part1.VERT, Part5.A1
  VCC: Part1.VCC, Part2.VCC, Part3.VCC, Part4.VCC, LCM1602_IIC2.VCC, U2.A0, U2.VCC, U1.VCC, R1.Pin_1, R2.Pin_1, R3.Pin_1, R4.Pin_1, R5.Pin_1, R6.Pin_1
  N4: Part2.SEL, Part5.D5_PWM
  N5: Part2.HORZ, Part5.A2
  N6: Part2.VERT, Part5.D4_PWM/A6
  N7: Part3.SEL, Part5.D8_PWM/A8
  N8: Part3.HORZ, Part5.D6_PWM/A7
  N9: Part3.VERT, Part5.A3
  N10: Part4.SEL, Part5.D9_PWM/A9
  N11: Part4.HORZ, Part5.A4
  N12: Part4.VERT, Part5.A5
  VSS: LCD2.VSS, LCM1602_IIC2.VSS
  VDD: LCD2.VDD, LCM1602_IIC2.VDD
  N13: LCD2.V0, LCM1602_IIC2.V0
  N14: LCD2.RS, LCM1602_IIC2.RS
  N15: LCD2.R/W, LCM1602_IIC2.RW
  N16: LCD2.E, LCM1602_IIC2.E
  N17: LCD2.DB0, LCM1602_IIC2.D0
  N18: LCD2.DB1, LCM1602_IIC2.D1
  N19: LCD2.DB2, LCM1602_IIC2.D2
  N20: LCD2.DB3, LCM1602_IIC2.D3
  N21: LCD2.DB4, LCM1602_IIC2.D4
  N22: LCD2.DB5, LCM1602_IIC2.D5
  N23: LCD2.DB6, LCM1602_IIC2.D6
  N24: LCD2.DB7, LCM1602_IIC2.D7
  N25: LCD2.LED+, LCM1602_IIC2.A
  N26: LCD2.LED-, LCM1602_IIC2.K
  N27: LCM1602_IIC2.SDA, Part5.D2/SDA, U2.SCL, U1.SCL
  N28: LCM1602_IIC2.SCL, Part5.D3/SCL, U2.SDA, U1.SDA
  N29: LCM1602_IIC2.LED_A, LCM1602_IIC2.LED_B
  N30: S1.leg0, U1.P0
  N31: Part5.D10_PWM/A10, S2.COM
  N32: U2.P0, S6.leg0
  N33: U2.P1, LED4.cathode
  N34: U2.P3, LED3.cathode
  N35: U2.INT, U1.INT
  N36: U1.P1, LED7.cathode
  N37: U1.P2, S3.leg0
  N38: U1.P3, LED2.cathode
  N39: U1.P4, S4.leg0
  N40: U1.P5, LED6.cathode
  N41: U1.P6, S5.leg0
  N42: U1.P7, LED5.cathode
  N43: LED3.anode, R1.Pin_0
  N44: LED4.anode, R3.Pin_0
  N45: LED5.anode, R2.Pin_0
  N46: LED6.anode, R6.Pin_0
  N47: LED7.anode, R5.Pin_0
  N48: LED2.anode, R4.Pin_0

notes:
  Joysticks 1
  Joysticks 2
  Joysticks 3
  Joysticks 4
  Arcade 1
  Arcade 2
  Arcade 3
  Arcade 4
  Arcade 5
  Arcade 6
  Ignition

custom parts:
  LCM1602 IIC: I2C-Module to use a 1602 or 2004 LCD on with the wire.h libory Serial LCD Modul
